// Logisim project cpu.circ as structural Verilog: 13 circuits, main circuit Main
module Somabits (
  input  a,
  input  b,
  input  cin,
  output s,
  output cout
);

  wire and_1_out, and_2_out, xor_1_out;

  xor xor_1 (xor_1_out, a, b);
  and and_1 (and_1_out, xor_1_out, cin);
  and and_2 (and_2_out, a, b);
  xor xor_2 (s, xor_1_out, cin);
  or or_1 (cout, and_1_out, and_2_out);

  // Notes on the sheet:
  //   O subcircuito somabits toma como inputs 2 bits, a e b, assim como um carry in ("cin"), e retorna o bit soma ("s"), assim como um bit carry out ("cout"). Esse subcircuito tem como funçao implementar a soma de dois bits.
endmodule

module Somador (
  input  [7:0] A,
  input  c0,
  input  [7:0] B,
  output [7:0] R,
  output C8
);

  wire somabits_1_cout, somabits_2_cout, somabits_3_cout, somabits_4_cout, somabits_5_cout, somabits_6_cout,
       somabits_7_cout;

  Somabits somabits_1 (.a(A[0]), .b(B[0]), .cin(c0), .s(R[0]), .cout(somabits_1_cout));
  Somabits somabits_2 (.a(A[1]), .b(B[1]), .cin(somabits_1_cout), .s(R[1]), .cout(somabits_2_cout));
  Somabits somabits_3 (.a(A[2]), .b(B[2]), .cin(somabits_2_cout), .s(R[2]), .cout(somabits_3_cout));
  Somabits somabits_4 (.a(A[3]), .b(B[3]), .cin(somabits_3_cout), .s(R[3]), .cout(somabits_4_cout));
  Somabits somabits_5 (.a(A[4]), .b(B[4]), .cin(somabits_4_cout), .s(R[4]), .cout(somabits_5_cout));
  Somabits somabits_6 (.a(A[5]), .b(B[5]), .cin(somabits_5_cout), .s(R[5]), .cout(somabits_6_cout));
  Somabits somabits_7 (.a(A[6]), .b(B[6]), .cin(somabits_6_cout), .s(R[6]), .cout(somabits_7_cout));
  Somabits somabits_8 (.a(A[7]), .b(B[7]), .cin(somabits_7_cout), .s(R[7]), .cout(C8));

  // Notes on the sheet:
  //   O subcircuito somador toma como inputs dois numeros de 8 bits ("A" e "B"), assim como o primeiro carry in ("c0"). Os outputs sao o numero de 8 bits R, assim como o carry out C8.
  //   Esse subcircuito tem como funçao implementar a soma de 2 numeros de 8 bits, usando os somabits em cascata.
endmodule

module Comparabits (
  input  enable,
  input  a,
  input  b,
  output a___b,
  output a___b_2,
  output a___b_3
);

  wire not_1_out, not_2_out, not_3_out, xor_1_out;

  not not_1 (not_1_out, b);
  not not_2 (not_2_out, a);
  xor xor_1 (xor_1_out, a, b);
  not not_3 (not_3_out, xor_1_out);
  and and_1 (a___b, enable, not_3_out);
  and and_2 (a___b_2, enable, a, not_1_out);
  and and_3 (a___b_3, enable, not_2_out, b);

  // Notes on the sheet:
  //   valor 1.
  //   O input enable é usado para possibilitar a comparação dos bits quando toma valor 1, ou forçar todas as 
  //   O subcircuito comparabits tem a função de comparar a magnitude de dois bits, nesse caso os inputs a e b. 
  //   saídas a anularem-se quando toma valor 0. Quando o enable é acionado, apenas um dos outputs retornará 
endmodule

module Comparador (
  input  [7:0] A,
  input  [7:0] B,
  output A___B,
  output A___B_2,
  output A___B_3
);

  wire comparabits_1_a___b, comparabits_1_a___b_2, comparabits_1_a___b_3, comparabits_2_a___b,
       comparabits_2_a___b_2, comparabits_2_a___b_3, comparabits_3_a___b, comparabits_3_a___b_2,
       comparabits_3_a___b_3, comparabits_4_a___b, comparabits_4_a___b_2, comparabits_4_a___b_3,
       comparabits_5_a___b, comparabits_5_a___b_2, comparabits_5_a___b_3, comparabits_6_a___b,
       comparabits_6_a___b_2, comparabits_6_a___b_3, comparabits_7_a___b, comparabits_7_a___b_2,
       comparabits_7_a___b_3, comparabits_8_a___b_2, comparabits_8_a___b_3;

  Comparabits comparabits_1 (
    .enable(1'b1), .a(A[7]), .b(B[7]), .a___b(comparabits_1_a___b), .a___b_2(comparabits_1_a___b_2),
    .a___b_3(comparabits_1_a___b_3));
  Comparabits comparabits_2 (
    .enable(comparabits_1_a___b), .a(A[6]), .b(B[6]), .a___b(comparabits_2_a___b),
    .a___b_2(comparabits_2_a___b_2), .a___b_3(comparabits_2_a___b_3));
  Comparabits comparabits_3 (
    .enable(comparabits_2_a___b), .a(A[5]), .b(B[5]), .a___b(comparabits_3_a___b),
    .a___b_2(comparabits_3_a___b_2), .a___b_3(comparabits_3_a___b_3));
  Comparabits comparabits_4 (
    .enable(comparabits_3_a___b), .a(A[4]), .b(B[4]), .a___b(comparabits_4_a___b),
    .a___b_2(comparabits_4_a___b_2), .a___b_3(comparabits_4_a___b_3));
  Comparabits comparabits_5 (
    .enable(comparabits_4_a___b), .a(A[3]), .b(B[3]), .a___b(comparabits_5_a___b),
    .a___b_2(comparabits_5_a___b_2), .a___b_3(comparabits_5_a___b_3));
  Comparabits comparabits_6 (
    .enable(comparabits_5_a___b), .a(A[2]), .b(B[2]), .a___b(comparabits_6_a___b),
    .a___b_2(comparabits_6_a___b_2), .a___b_3(comparabits_6_a___b_3));
  Comparabits comparabits_7 (
    .enable(comparabits_6_a___b), .a(A[1]), .b(B[1]), .a___b(comparabits_7_a___b),
    .a___b_2(comparabits_7_a___b_2), .a___b_3(comparabits_7_a___b_3));
  Comparabits comparabits_8 (
    .enable(comparabits_7_a___b), .a(A[0]), .b(B[0]), .a___b(A___B_2), .a___b_2(comparabits_8_a___b_2),
    .a___b_3(comparabits_8_a___b_3));
  or or_1 (A___B, comparabits_1_a___b_2, comparabits_2_a___b_2, comparabits_3_a___b_2, comparabits_4_a___b_2, comparabits_5_a___b_2, comparabits_6_a___b_2, comparabits_7_a___b_2, comparabits_8_a___b_2);
  or or_2 (A___B_3, comparabits_8_a___b_3, comparabits_7_a___b_3, comparabits_6_a___b_3, comparabits_5_a___b_3, comparabits_4_a___b_3, comparabits_3_a___b_3, comparabits_2_a___b_3, comparabits_1_a___b_3);

  // Notes on the sheet:
  //   O subcircuito comparador tem a função de comparar o valor absoluto de dois numeros binários de 8 bits, denotados por A e B.
  //   Ele consiste na implementação em cascata do subcircuito comparabits e retorna valor 1 para apenas um de seus outputs.
endmodule

module ULA (
  input  [7:0] A,
  input  OP,
  input  [7:0] B,
  output Overflow,
  output [7:0] R,
  output A___B,
  output A___B_2,
  output A___B_3
);

  wire somador_1_c8;
  wire [7:0] xor_1_out;

  xor xor_1 (xor_1_out[0], B[0], OP);
  xor xor_2 (xor_1_out[1], B[1], OP);
  xor xor_3 (xor_1_out[2], B[2], OP);
  xor xor_4 (xor_1_out[3], B[3], OP);
  xor xor_5 (xor_1_out[4], B[4], OP);
  xor xor_6 (xor_1_out[5], B[5], OP);
  xor xor_7 (xor_1_out[6], B[6], OP);
  xor xor_8 (xor_1_out[7], B[7], OP);
  Somador somador_1 (.A(A), .c0(OP), .B(xor_1_out), .R(R), .C8(somador_1_c8));
  Comparador comparador_1 (.A(A), .B(B), .A___B(A___B), .A___B_2(A___B_2), .A___B_3(A___B_3));
  xor xor_9 (Overflow, OP, somador_1_c8);

  // Notes on the sheet:
  //    A ULA é responsável por receber dois números binários de 8 bits, A e B, e efetuar a adição ou subtração desses números, assim como comparar os seus valores absolutos.
  //   Se o valor do input OP for nulo, o circuito retornará o valor da adição no output R, enquanto que se OP for igual a 1, o circuito retornará o valor da subtração no output R. Os três outputs provenientes
  //   do comparador indicam se A > B,   A < B ou A = B, de modo que sempre somente um deles toma valor 1. Todas as operações são feitas considerando a interpretação sem sinal dos números A e B.
endmodule

module AC (
  input  [7:0] Entrada_para_ULA,
  input  [15:0] Entrada_para_RAM,
  input  controle_de_entrada,
  input  AC_enable,
  input  Clock,
  input  Reset_do_AC,
  output [15:0] \Saída_para_RAM ,
  output [7:0] \Saída_para_ULA ,
  output [7:0] Valor_do_AC,
  output [7:0] UC
);

  wire [7:0] bitselector_1_out, multiplexer_1_out;

  BitSelector #(.width(16), .group(8)) bitselector_1 (.in(Entrada_para_RAM), .out(bitselector_1_out), .sel(1'b0));
  Multiplexer #(.width(8)) multiplexer_1 (
    .in0(Entrada_para_ULA), .in1(bitselector_1_out), .out(multiplexer_1_out), .sel(controle_de_entrada));  // open: en
  Register register_1 (.D(multiplexer_1_out), .en(AC_enable), .Q(\Saída_para_ULA ), .clk(Clock), .clr(Reset_do_AC));
  assign \Saída_para_RAM  = {{8{1'b0}}, \Saída_para_ULA };  // Bit_Extender bit_extender_1

  assign UC = \Saída_para_ULA ;
  assign Valor_do_AC = \Saída_para_ULA ;

  // Notes on the sheet:
  //   O subcircuito AC tem a função de guardar valores contidos na RAM, assim como interagir com a ULA para realizar operações aritméticas.
  //   Além disso, ele pode escrever o valor contido em seu registrador na RAM, assim como enviá-lo para a UC, onde serão feitos testes de
  //   desvio condicional. O registrador do AC só será atualizado no pulso de clock do Execute se o bit de controle "AC enable" tomar valor 1. 
endmodule

module PC (
  input  [7:0] \Endereço_vindo_do_IR ,
  input  Reset,
  input  end_inc,
  input  Clock,
  output [7:0] RAM
);

  wire not_1_out;
  wire [7:0] counter_1_q;

  not not_1 (not_1_out, end_inc);
  Counter counter_1 (
    .load(not_1_out), .D(\Endereço_vindo_do_IR ), .count(end_inc), .Q(counter_1_q), .clk(Clock), .clr(Reset));  // open: carry
  Multiplexer #(.width(8)) multiplexer_1 (
    .in0(\Endereço_vindo_do_IR ), .in1(counter_1_q), .out(RAM), .sel(Clock));  // open: en

  // Notes on the sheet:
  //   próxima instrução a ser copiada pelo IR no pulso do fetch.
  //   Bit que controla se o PC fará um incremento simples da
  //   sequência de instruções do programa, ou um desvio.
  //   O subcircuito PC tem a função de controlar a mudança de endereços da RAM de maneira apropriada. Ele foi constrído de modo a alternar entre o endereço vindo da instrução sendo realizada no ciclo atual 
  //   e o endereço da instrução do programa sendo executado. No decode, a saída do PC será o endereço contido na instrução, enquanto que, no momento anterior ao fetch, a saída do PC será o endereço da
endmodule

module UC (
  input  [15:0] Valor_da_RAM_vindo_do_IR,
  input  [3:0] in_2,
  input  [7:0] AC_value,
  output end_inc,
  output Reset,
  output AC_enable,
  output Entrada_para_AC,
  output read___write,
  output Printer_enable,
  output ULA_operation,
  output Entrada_manual___AC
);

  wire and_1_out, decoder_1_out0, decoder_2_out0, not_1_out;
  wire [3:0] bitselector_2_out, bitselector_3_out, \Instrução ;

  BitSelector #(.width(16), .group(4)) bitselector_1 (.in(Valor_da_RAM_vindo_do_IR), .out(\Instrução ), .sel(2'b10));
  and and_1 (and_1_out, decoder_1_out0, decoder_2_out0);
  Decoder #(.select(4)) decoder_1 (
    .out0(decoder_1_out0), .sel(bitselector_2_out));  // open: out1, out2, out3, out4, out5, out6, out7, out8, out9, out10, out11, out12, out13, out14, out15, en
  Decoder #(.select(4)) decoder_2 (
    .out0(decoder_2_out0), .sel(bitselector_3_out));  // open: out1, out2, out3, out4, out5, out6, out7, out8, out9, out10, out11, out12, out13, out14, out15, en
  BitSelector #(.group(4)) bitselector_2 (.in(AC_value), .out(bitselector_2_out), .sel(1'b0));
  BitSelector #(.group(4)) bitselector_3 (.in(AC_value), .out(bitselector_3_out), .sel(1'b1));
  Multiplexer #(.select(4)) multiplexer_1 (
    .in0(1'b1), .in1(1'b1), .in2(1'b1), .in3(1'b1), .in4(1'b1), .in7(1'b1), .in8(1'b1), .in9(1'b1),
    .in10(1'b0), .in11(and_1_out), .in13(not_1_out), .out(end_inc), .sel(in_2));  // open: in5, in6, in12, in14, in15, en
  not not_1 (not_1_out, and_1_out);
  Multiplexer #(.select(4)) multiplexer_2 (
    .in0(1'b0), .in1(1'b0), .in2(1'b1), .in3(1'b0), .in4(1'b0), .in7(1'b1), .in8(1'b0), .in9(1'b0),
    .in10(1'b0), .in11(1'b0), .in13(1'b0), .out(read___write), .sel(in_2));  // open: in5, in6, in12, in14, in15, en
  Multiplexer #(.select(4)) multiplexer_3 (
    .in0(1'b0), .in1(1'b0), .in2(1'b0), .in3(1'b0), .in4(1'b0), .in7(1'b0), .in8(1'b0), .in9(1'b1),
    .in10(1'b0), .in11(1'b0), .in13(1'b0), .out(Reset), .sel(in_2));  // open: in5, in6, in12, in14, in15, en
  Multiplexer #(.select(4)) multiplexer_4 (
    .in0(1'b0), .in1(1'b0), .in2(1'b0), .in3(1'b0), .in4(1'b0), .in7(1'b0), .in8(1'b1), .in9(1'b0),
    .in10(1'b0), .in11(1'b0), .in13(1'b0), .out(Printer_enable), .sel(\Instrução ));  // open: in5, in6, in12, in14, in15, en
  Multiplexer #(.select(4)) multiplexer_5 (
    .in0(1'b0), .in1(1'b1), .in2(1'b0), .in3(1'b1), .in4(1'b1), .in7(1'b0), .in8(1'b0), .in9(1'b0),
    .in10(1'b0), .in11(1'b0), .in13(1'b0), .out(AC_enable), .sel(in_2));  // open: in5, in6, in12, in14, in15, en
  Multiplexer #(.select(4)) multiplexer_6 (
    .in0(1'b0), .in1(1'b0), .in2(1'b0), .in3(1'b0), .in4(1'b1), .in7(1'b0), .in8(1'b0), .in9(1'b0),
    .in10(1'b0), .in11(1'b0), .in13(1'b0), .out(ULA_operation), .sel(\Instrução ));  // open: in5, in6, in12, in14, in15, en
  Multiplexer #(.select(4)) multiplexer_7 (
    .in0(1'b1), .in1(1'b1), .in2(1'b1), .in3(1'b0), .in4(1'b0), .in7(1'b1), .in8(1'b1), .in9(1'b1),
    .in10(1'b1), .in11(1'b1), .in13(1'b1), .out(Entrada_para_AC), .sel(in_2));  // open: in5, in6, in12, in14, in15, en
  Multiplexer #(.select(4)) multiplexer_8 (
    .in0(1'b1), .in1(1'b1), .in2(1'b1), .in3(1'b1), .in4(1'b1), .in7(1'b0), .in8(1'b1), .in9(1'b1),
    .in10(1'b1), .in11(1'b1), .in13(1'b1), .out(Entrada_manual___AC), .sel(\Instrução ));  // open: in5, in6, in12, in14, in15, en

  // Notes on the sheet:
  //   Controle de desvio / incremento
  //   Essa porta AND toma valor de saída 1 apenas quando o valor 
  //   contido no AC é 00000000, caso contrário ela tomará valor 0.
  //   Entrada / saída da RAM
  //   Essas variáveis tomam os valores dos bits da instrução sendo excutada no ciclo atual.
  //   Reset do valor do PC,
  //   do AC e do Printer.
  //   Bit para a intrução de print
  //   A UC foi construída de modo que cada bit de controle corresponde a uma função booleana em quatro variáveis, cada uma implementada com um multiplexador. 
  //   necessidade.
  //   Bloqueio do AC para impedir que
  //   o valor contido seja alterado sem
  //   Soma / Subtração
  //   Alternância entre entrada
  //   Entrada da ULA ou da RAM
  //   no AC.
  //   manual ou do valor contido
  //   no AC na escrita na RAM.
endmodule

module Print8 (
  input  [7:0] _8_bits,
  output [3:0] d1,
  output [3:0] d0
);

  BitSelector #(.group(4)) bitselector_1 (.in(_8_bits), .out(d1), .sel(1'b1));
  BitSelector #(.group(4)) bitselector_2 (.in(_8_bits), .out(d0), .sel(1'b0));

  // Notes on the sheet:
  //   Circuito criado para mostrar os valores contidos no AC e no Printer.
endmodule

module Printer (
  input  [15:0] Entrada_para_a_RAM,
  input  Enable_do_Printer,
  input  Clock,
  input  Reset,
  output [3:0] d1,
  output [3:0] d0
);

  wire [7:0] bitselector_1_out, register_1_q;

  BitSelector #(.width(16), .group(8)) bitselector_1 (.in(Entrada_para_a_RAM), .out(bitselector_1_out), .sel(1'b0));
  Register register_1 (.D(bitselector_1_out), .en(Enable_do_Printer), .Q(register_1_q), .clk(Clock), .clr(Reset));
  Print8 print8 (._8_bits(register_1_q), .d1(d1), .d0(d0));

  // Notes on the sheet:
  //   Subcircuito criado para realizar a impressão de valores da memória RAM. O registrador será ativado apenas quando a instrução 08 entrar no UC.
endmodule

module Distribuidor (
  input  Entrada_manual___AC,
  input  [7:0] Entrada_manual_para_RAM,
  input  [15:0] AC_para_RAM,
  input  [15:0] Leitura_da_RAM,
  input  [15:0] \endereço_do_IR_para_PC ,
  output [15:0] Entrada_manual___AC_para_RAM,
  output [7:0] RAM_para_ULA,
  output [15:0] RAM_para_AC,
  output [15:0] RAM_para_printer,
  output [7:0] \Endereço_para_PC 
);

  wire [15:0] bit_extender_1_out;

  assign bit_extender_1_out = {{8{1'b0}}, Entrada_manual_para_RAM};  // Bit_Extender bit_extender_1
  BitSelector #(.width(16), .group(8)) bitselector_1 (
    .in(\endereço_do_IR_para_PC ), .out(\Endereço_para_PC ), .sel(1'b0));
  Multiplexer #(.width(16)) multiplexer_1 (
    .in0(bit_extender_1_out), .in1(AC_para_RAM), .out(Entrada_manual___AC_para_RAM), .sel(Entrada_manual___AC));  // open: en
  BitSelector #(.width(16), .group(8)) bitselector_2 (.in(Leitura_da_RAM), .out(RAM_para_ULA), .sel(1'b0));

  assign RAM_para_AC = Leitura_da_RAM;
  assign RAM_para_printer = Leitura_da_RAM;

  // Notes on the sheet:
  //   Esse subcircuito foi criado para modularizar o circuito main, tornando-o mais compacto e inteligível.
  //   Bit de controle de escrita na RAM
endmodule

module Habilitador (
  input  \Reset_da_instrução_09 ,
  input  reset___enable,
  output reset_do_Printer,
  output reset_do_AC,
  output Reset_do_PC,
  output reset_do_IR,
  output reset_do_Flip_Flop,
  output bloqueio_da_RAM
);

  Multiplexer multiplexer_1 (
    .in0(1'b1), .in1(\Reset_da_instrução_09 ), .out(Reset_do_PC), .sel(reset___enable));  // open: en
  not not_1 (reset_do_Flip_Flop, reset___enable);
  Multiplexer multiplexer_2 (
    .in0(1'b1), .in1(\Reset_da_instrução_09 ), .out(reset_do_AC), .sel(reset___enable));  // open: en
  Multiplexer multiplexer_3 (
    .in0(1'b1), .in1(\Reset_da_instrução_09 ), .out(reset_do_Printer), .sel(reset___enable));  // open: en

  assign bloqueio_da_RAM = reset___enable;
  assign reset_do_IR = reset_do_Flip_Flop;

  // Notes on the sheet:
  //   Esse subcircuito foi criado para lidar com o problema das partes sequenciais do circuito, como o contador do PC e o IR, serem alterados na ausência de qualquer 
  //   programa na memória RAM sendo executado. Para evitar esse problema, esse subcircuito bloqueia a RAM e reseta os valores da parte sequencial do circuito.
  //   Dessa forma, os componentes sequenciais não serão desconfigurados com pulsos de clock que ocorram no momento anterior ou posterior à execução do programa.
endmodule

module Main (
  input  Habilitador___resetador_do_circuito,
  input  [7:0] Entrada_manual_de_dados
);

  wire AC_enable, bloqueio_da_RAM, Clock1, Clock2, Clock_global_out, end___inc, Entrada_manual___AC,
       Entrada_para_AC, Printer_enable, read___write, reset_do_AC, reset_do_Flip_Flop, reset_do_IR,
       reset_do_PC, reset_do_Printer, \Reset_via_instrução_09 , ULA_operation;
  wire [3:0] print8_d0, print8_d1, printer_1_d0, printer_1_d1;
  wire [7:0] \ac_1_saída_para_ula , ac_1_valor_do_ac, AC_para_o_UC, \Distribuidor_endereço_para_pc ,
       Distribuidor_ram_para_ula, pc_1_ram, ula_1_r;
  wire [15:0] \ac_1_saída_para_ram , Distribuidor_entrada_manual___ac_para_ram, Distribuidor_ram_para_ac,
       Distribuidor_ram_para_printer, \Instrução_para_o_UC , ram_1_data;

  Hex_Digit_Display hex_digit_display_1 (.value(printer_1_d0));  // open: dp
  Hex_Digit_Display hex_digit_display_2 (.value(printer_1_d1));  // open: dp
  PC pc_1 (
    .\Endereço_vindo_do_IR (\Distribuidor_endereço_para_pc ), .Clock(Clock2), .end_inc(end___inc),
    .Reset(reset_do_PC), .RAM(pc_1_ram));
  Printer printer_1 (
    .Entrada_para_a_RAM(Distribuidor_ram_para_printer), .d1(printer_1_d1), .d0(printer_1_d0),
    .Enable_do_Printer(Printer_enable), .Reset(reset_do_Printer), .Clock(Clock2));
  Habilitador Habilitador (
    .\Reset_da_instrução_09 (\Reset_via_instrução_09 ), .reset___enable(Habilitador___resetador_do_circuito),
    .reset_do_Printer(reset_do_Printer), .reset_do_AC(reset_do_AC), .Reset_do_PC(reset_do_PC),
    .reset_do_IR(reset_do_IR), .reset_do_Flip_Flop(reset_do_Flip_Flop), .bloqueio_da_RAM(bloqueio_da_RAM));
  Distribuidor Distribuidor (
    .Entrada_manual_para_RAM(Entrada_manual_de_dados), .AC_para_RAM(\ac_1_saída_para_ram ),
    .Leitura_da_RAM(ram_1_data), .\endereço_do_IR_para_PC (\Instrução_para_o_UC ),
    .Entrada_manual___AC(Entrada_manual___AC),
    .Entrada_manual___AC_para_RAM(Distribuidor_entrada_manual___ac_para_ram),
    .RAM_para_ULA(Distribuidor_ram_para_ula), .RAM_para_AC(Distribuidor_ram_para_ac),
    .RAM_para_printer(Distribuidor_ram_para_printer), .\Endereço_para_PC (\Distribuidor_endereço_para_pc ));
  AC ac_1 (
    .Entrada_para_ULA(ula_1_r), .Entrada_para_RAM(Distribuidor_ram_para_ac),
    .controle_de_entrada(Entrada_para_AC), .AC_enable(AC_enable), .Clock(Clock2), .Reset_do_AC(reset_do_AC),
    .\Saída_para_RAM (\ac_1_saída_para_ram ), .\Saída_para_ULA (\ac_1_saída_para_ula ),
    .Valor_do_AC(ac_1_valor_do_ac), .UC(AC_para_o_UC));
  UC uc_1 (
    .Valor_da_RAM_vindo_do_IR(\Instrução_para_o_UC ), .AC_value(AC_para_o_UC), .end_inc(end___inc),
    .Reset(\Reset_via_instrução_09 ), .AC_enable(AC_enable), .Entrada_para_AC(Entrada_para_AC),
    .read___write(read___write), .Printer_enable(Printer_enable), .ULA_operation(ULA_operation),
    .Entrada_manual___AC(Entrada_manual___AC));  // open: in_2
  RAM #(.dataWidth(16), .bus("separate")) ram_1 (
    .addr(pc_1_ram), .din(Distribuidor_entrada_manual___ac_para_ram), .data(ram_1_data), .str(read___write),
    .sel(bloqueio_da_RAM), .clk(Clock2));  // open: ld, clr
  ULA ula_1 (
    .A(\ac_1_saída_para_ula ), .OP(ULA_operation), .B(Distribuidor_ram_para_ula), .R(ula_1_r));  // open: A___B_2, A___B_3, Overflow, A___B
  Register #(.width(16)) IR (.D(ram_1_data), .Q(\Instrução_para_o_UC ), .clk(Clock1), .clr(reset_do_IR));  // open: en
  Print8 print8 (._8_bits(ac_1_valor_do_ac), .d1(print8_d1), .d0(print8_d0));
  Hex_Digit_Display hex_digit_display_3 (.value(print8_d1));  // open: dp
  Hex_Digit_Display hex_digit_display_4 (.value(print8_d0));  // open: dp
  Clock Clock_global (.out(Clock_global_out));
  J_K_Flip_Flop j_k_ff_1 (
    .J(1'b1), .clk(Clock_global_out), .K(1'b1), .Q(Clock2), .Qn(Clock1), .preset(reset_do_Flip_Flop));  // open: en, reset

  // Notes on the sheet:
  //   recomeçar manualmente a execução do programa.
  //   Antes de começar a execução do programa, por favor ative o bit 
  //   ao lado. Esse bit também pode ser usado caso seja necessário
  //   Print
  //   Valor contido no AC
  //   O circuito funciona com dois pulsos de clock global por ciclo.
endmodule
